# Fritzing sketch PCB_rev2 (saved by Fritzing 0.9.3b)
circuit board: 8.8cm x 5.4cm
breadboards: 1

parts:
  J24 = female pin header, 7 pins [form="♀ (female)"]
  J25 = female pin header, 7 pins [form="♀ (female)"]
  J26 = female pin header, 3 pins [form="♀ (female)"]
  J27 = female pin header, 3 pins [form="♀ (female)"]
  J28 = female pin header, 3 pins [form="♀ (female)"]
  J29 = female pin header, 3 pins [form="♀ (female)"]
  J21 = female pin header, 8 pins [form="♀ (female)"]
  J22 = female pin header, 8 pins [form="♀ (female)"]
  J30 = female pin header, 4 pins [form="♀ (female)"]
  A1 = Esp32-c3 super mini  # not connected
  J31 = female pin header, 2 pins [form="♀ (female)"]
  J32 = female pin header, 2 pins [form="♀ (female)"]

nets:
  N1: J24.pin1, J25.pin1, J26.pin3, J27.pin3, J28.pin3, J21.pin6, J30.pin1
  N2: J24.pin2, J25.pin2, J26.pin1, J27.pin1, J28.pin1, J29.pin2, J21.pin7, J30.pin2, J31.pin2, J32.pin1
  N3: J24.pin3, J25.pin3, J21.pin5
  N4: J24.pin4, J25.pin4, J22.pin7
  N5: J24.pin5, J25.pin5, J21.pin2
  N6: J24.pin6, J21.pin3
  N7: J24.pin7, J25.pin7, J32.pin2
  N8: J25.pin6, J21.pin4
  N9: J26.pin2, J22.pin6
  N10: J27.pin2, J21.pin1
  N11: J28.pin2, J22.pin3
  N12: J29.pin3, J22.pin8
  N13: J21.pin8, J31.pin1
  N14: J22.pin4, J30.pin3
  N15: J22.pin5, J30.pin4

notes:
  V I G
  VCC
  GND
  SCL
  SDA
  DC
  RST
  CS
  TFT_1
  TFT_2
  ESP32C3SM
  SAQ
  JLCJLCJLCJLC
  5V
  TFT_1_UI_btn
  TFT_2_UI_btn
  TFT_brightness_btn
  Exit_serial_sw
  cable routing
  hole

custom parts:
  Esp32-c3 super mini: ESP32-C3 Development Board ESP32 SuperMini Development Board ESP32 Development Board WiFi Bluetooth.
